# Fritzing sketch TemperatureI2C (saved by Fritzing 0.9.3b)
breadboards: 1

parts:
  Part1 = Arduino Uno (Rev3)
  Raspberry_Pi_1 = Raspberry Pi 3 [part_number=RPI-3-V1.2]
  T1 = LM35 Temperature Sensor [package="TO92 [THT]"]

nets:
  N1: Part1.A0, T1.Vout
  N2: Part1.A4/SDA, Raspberry_Pi_1.GPIO2
  N3: Part1.A5/SCL, Raspberry_Pi_1.GPIO3
  N4: Part1.5V, T1.+Vs
  GND: Part1.GND, Raspberry_Pi_1.GND, T1.GND
